# Fritzing sketch hx711 (saved by Fritzing 0.9.3b)
breadboards: 1

parts:
  Componente1 = HX711 Weighing Sensor Module
  Componente2 = Arduino Uno (Rev3)

nets:
  VCC: Componente1.VCC, Componente2.5V
  GND: Componente1.GND, Componente2.GND
  N1: Componente1.DO/RX, Componente2.A4/SDA
  N2: Componente1.CK/TX, Componente2.A5/SCL

notes:
  Load Cell
  E+ (RED)
  E- (BLACK)
  A- (WHITE)
  A+ (GREEN)
